# Fritzing sketch clock_protoboard (saved by Fritzing 0.9.9b)
circuit board: 13.7519cm x 3.60632cm
stripboards: 1

parts:
  ZS-042_RTC1 = ZS-042 RTC Module
  U1 = ATTINY45 [package=dip]
  Sminus = Pushbutton [package="[THT]"]
  Smode = Pushbutton [package="[THT]"]
  M1 = MAX7219 8x8 single Led Matrix Module
  M2 = MAX7219 8x8 single Led Matrix Module
  M3 = MAX7219 8x8 single Led Matrix Module
  R1 = Resistor [tolerance=±5% resistance=10k power=0.25 package=THT]
  R3 = Resistor [tolerance=±5% resistance=56k power=0.25 package=THT]
  J1 = female pin header, 5 pins [form="♀ (female)"]
  J2 = male pin header, 5 pins [form="♂ (male)"]
  C2 = Ceramic Capacitor [capacitance=100nF voltage=10V package="100 mil [THT, multilayer]"]
  Sreset = Pushbutton [package="[THT]"]
  Splus = Pushbutton [package="[THT]"]
  R2 = Resistor [tolerance=±5% resistance=10k power=0.25 package=THT]
  C1 = Electrolytic Capacitor [capacitance=100µF voltage=35V package="100 mil [THT, electrolytic]"]
  J6 = male pin header, 4 pins [form="♂ (male)"]
  J7 = female pin header, 4 pins [form="♀ (female)"]

nets:
  GND/J4/J9: ZS-042_RTC1.GND, U1.GND, M1.I-GND-1, M1.O-GND-1, M1.I-GND-2, M1.O-GND-2, M1.I-GND-3, M1.O-GND-3, M1.I-GND-4, M1.O-GND-4, M2.I-GND-1, M2.O-GND-1, M2.I-GND-2, M2.O-GND-2, M2.I-GND-3, M2.O-GND-3, M2.I-GND-4, M2.O-GND-4, M3.I-GND-1, M3.O-GND-1, M3.I-GND-2, M3.O-GND-2, M3.I-GND-3, M3.O-GND-3, M3.I-GND-4, M3.O-GND-4, R3.Pin_0, J1.pin4, J2.pin4, C2.0, Sreset.Pin_3, Sreset.Pin_4, C1.-, J6.pin4, J7.pin4
  5V/J5/J8: ZS-042_RTC1.VCC, U1.VCC, Smode.Pin_1, Smode.Pin_2, M1.I-VCC-1, M1.O-VCC-1, M1.I-VCC-2, M1.O-VCC-2, M1.I-VCC-3, M1.O-VCC-3, M1.I-VCC-4, M1.O-VCC-4, M2.I-VCC-1, M2.O-VCC-1, M2.I-VCC-2, M2.O-VCC-2, M2.I-VCC-3, M2.O-VCC-3, M2.I-VCC-4, M2.O-VCC-4, M3.I-VCC-1, M3.O-VCC-1, M3.I-VCC-2, M3.O-VCC-2, M3.I-VCC-3, M3.O-VCC-3, M3.I-VCC-4, M3.O-VCC-4, J1.pin5, J2.pin5, C2.1, R2.Pin_1, C1.+, J6.pin3, J7.pin3
  J3/J7: ZS-042_RTC1.SDA, U1.PB0(MOSI), M3.I-DIN-1, J1.pin3, J2.pin3, J6.pin2, J7.pin2
  J6: ZS-042_RTC1.SCL, U1.PB2(SCK_ADC1), J6.pin1, J7.pin1
  N1: U1.PB5(NRES), Sreset.Pin_1, Sreset.Pin_2
  N2: U1.PB3(ADC3), Sminus.Pin_3, Sminus.Pin_4, Smode.Pin_3, Smode.Pin_4, R3.Pin_1, Splus.Pin_3, Splus.Pin_4
  J2: U1.PB4(ADC2), M1.I-CS-1, M1.O-CS-1, M1.I-CS-2, M1.O-CS-2, M1.I-CS-3, M1.O-CS-3, M1.I-CS-4, M1.O-CS-4, M2.I-CS-1, M2.O-CS-1, M2.I-CS-2, M2.O-CS-2, M2.I-CS-3, M2.O-CS-3, M2.I-CS-4, M2.O-CS-4, M3.I-CS-1, M3.O-CS-1, M3.I-CS-2, M3.O-CS-2, M3.I-CS-3, M3.O-CS-3, M3.I-CS-4, M3.O-CS-4, J1.pin2, J2.pin2
  J1: U1.PB1(MISO), M1.I-CLK-1, M1.O-CLK-1, M1.I-CLK-2, M1.O-CLK-2, M1.I-CLK-3, M1.O-CLK-3, M1.I-CLK-4, M1.O-CLK-4, M2.I-CLK-1, M2.O-CLK-1, M2.I-CLK-2, M2.O-CLK-2, M2.I-CLK-3, M2.O-CLK-3, M2.I-CLK-4, M2.O-CLK-4, M3.I-CLK-1, M3.O-CLK-1, M3.I-CLK-2, M3.O-CLK-2, M3.I-CLK-3, M3.O-CLK-3, M3.I-CLK-4, M3.O-CLK-4, J1.pin1, J2.pin1
  N3: Sminus.Pin_1, Sminus.Pin_2, R1.Pin_0
  N4: M1.I-DIN-1, M3.O-DOUT-4
  N5: M1.O-DOUT-1, M1.I-DIN-2
  N6: M1.O-DOUT-2, M1.I-DIN-3
  N7: M1.O-DOUT-3, M1.I-DIN-4
  N8: M1.O-DOUT-4, M2.I-DIN-1
  N9: M2.O-DOUT-1, M2.I-DIN-2
  N10: M2.O-DOUT-2, M2.I-DIN-3
  N11: M2.O-DOUT-3, M2.I-DIN-4
  N12: M3.O-DOUT-1, M3.I-DIN-2
  N13: M3.O-DOUT-2, M3.I-DIN-3
  N14: M3.O-DOUT-3, M3.I-DIN-4
  N15: R1.Pin_1, Splus.Pin_1, Splus.Pin_2, R2.Pin_0

custom parts:
  MAX7219 8x8 single Led Matrix Module: Description: MAX7219 8x8 LedMatrix single Red Module Dimensions: 32x32mm Documents:
