# Fritzing sketch clock (saved by Fritzing 0.9.9b)
circuit board: 13.7519cm x 3.60632cm
breadboards: 1
stripboards: 1

parts:
  ZS-042_RTC1 = ZS-042 RTC Module
  U1 = ATTINY45 [package=dip]
  Sminus = Pushbutton [package="[THT]"]
  Splus = Pushbutton [package="[THT]"]
  Smode = Pushbutton [package="[THT]"]
  M1 = MAX7219 8x8 single Led Matrix Module
  M2 = MAX7219 8x8 single Led Matrix Module
  M3 = MAX7219 8x8 single Led Matrix Module
  R1 = Resistor [tolerance=±5% resistance=10k package=THT]
  R2 = Resistor [tolerance=±5% resistance=10k package=THT]
  R3 = Resistor [tolerance=±5% resistance=56k package=THT]
  J1 = female pin header, 5 pins [form="♀ (female)"]
  J2 = male pin header, 5 pins [form="♂ (male)"]
  C1 = Electrolytic Capacitor [capacitance=10µF voltage=35V package="100 mil [THT, electrolytic]"]
  C2 = Ceramic Capacitor [capacitance=100nF voltage=10V package="100 mil [THT, multilayer]"]
  Sreset = Pushbutton [package="[THT]"]

nets:
  GND/J4: ZS-042_RTC1.GND, U1.GND, M1.I-GND-1, M1.O-GND-1, M1.I-GND-2, M1.O-GND-2, M1.I-GND-3, M1.O-GND-3, M1.I-GND-4, M1.O-GND-4, M2.I-GND-1, M2.O-GND-1, M2.I-GND-2, M2.O-GND-2, M2.I-GND-3, M2.O-GND-3, M2.I-GND-4, M2.O-GND-4, M3.I-GND-1, M3.O-GND-1, M3.I-GND-2, M3.O-GND-2, M3.I-GND-3, M3.O-GND-3, M3.I-GND-4, M3.O-GND-4, R3.Pin_0, J1.pin4, J2.pin4, C1.-, C2.0, Sreset.Pin_3, Sreset.Pin_4
  5V/J5: ZS-042_RTC1.VCC, U1.VCC, Smode.Pin_1, Smode.Pin_2, M1.I-VCC-1, M1.O-VCC-1, M1.I-VCC-2, M1.O-VCC-2, M1.I-VCC-3, M1.O-VCC-3, M1.I-VCC-4, M1.O-VCC-4, M2.I-VCC-1, M2.O-VCC-1, M2.I-VCC-2, M2.O-VCC-2, M2.I-VCC-3, M2.O-VCC-3, M2.I-VCC-4, M2.O-VCC-4, M3.I-VCC-1, M3.O-VCC-1, M3.I-VCC-2, M3.O-VCC-2, M3.I-VCC-3, M3.O-VCC-3, M3.I-VCC-4, M3.O-VCC-4, R2.Pin_1, J1.pin5, J2.pin5, C1.+, C2.1
  J3: ZS-042_RTC1.SDA, U1.PB0(MOSI), M1.I-DIN-1, J1.pin3, J2.pin3
  N1: ZS-042_RTC1.SCL, U1.PB2(SCK_ADC1)
  N2: U1.PB5(NRES), Sreset.Pin_1, Sreset.Pin_2
  N3: U1.PB3(ADC3), Sminus.Pin_3, Sminus.Pin_4, Splus.Pin_3, Splus.Pin_4, Smode.Pin_3, Smode.Pin_4, R3.Pin_1
  J2: U1.PB4(ADC2), M1.I-CS-1, M1.O-CS-1, M1.I-CS-2, M1.O-CS-2, M1.I-CS-3, M1.O-CS-3, M1.I-CS-4, M1.O-CS-4, M2.I-CS-1, M2.O-CS-1, M2.I-CS-2, M2.O-CS-2, M2.I-CS-3, M2.O-CS-3, M2.I-CS-4, M2.O-CS-4, M3.I-CS-1, M3.O-CS-1, M3.I-CS-2, M3.O-CS-2, M3.I-CS-3, M3.O-CS-3, M3.I-CS-4, M3.O-CS-4, J1.pin2, J2.pin2
  J1: U1.PB1(MISO), M1.I-CLK-1, M1.O-CLK-1, M1.I-CLK-2, M1.O-CLK-2, M1.I-CLK-3, M1.O-CLK-3, M1.I-CLK-4, M1.O-CLK-4, M2.I-CLK-1, M2.O-CLK-1, M2.I-CLK-2, M2.O-CLK-2, M2.I-CLK-3, M2.O-CLK-3, M2.I-CLK-4, M2.O-CLK-4, M3.I-CLK-1, M3.O-CLK-1, M3.I-CLK-2, M3.O-CLK-2, M3.I-CLK-3, M3.O-CLK-3, M3.I-CLK-4, M3.O-CLK-4, J1.pin1, J2.pin1
  N4: Sminus.Pin_1, Sminus.Pin_2, R1.Pin_0
  N5: Splus.Pin_1, Splus.Pin_2, R1.Pin_1, R2.Pin_0
  N6: M1.O-DOUT-1, M1.I-DIN-2
  N7: M1.O-DOUT-2, M1.I-DIN-3
  N8: M1.O-DOUT-3, M1.I-DIN-4
  N9: M1.O-DOUT-4, M2.I-DIN-1
  N10: M2.O-DOUT-1, M2.I-DIN-2
  N11: M2.O-DOUT-2, M2.I-DIN-3
  N12: M2.O-DOUT-3, M2.I-DIN-4
  N13: M2.O-DOUT-4, M3.I-DIN-1
  N14: M3.O-DOUT-1, M3.I-DIN-2
  N15: M3.O-DOUT-2, M3.I-DIN-3
  N16: M3.O-DOUT-3, M3.I-DIN-4

custom parts:
  MAX7219 8x8 single Led Matrix Module: Description: MAX7219 8x8 LedMatrix single Red Module Dimensions: 32x32mm Documents:
