# Fritzing sketch clock_protoboard (saved by Fritzing 0.9.9b)
circuit board: 13.7519cm x 3.60632cm
stripboards: 2

parts:
  ZS-042_RTC1 = ZS-042 RTC Module
  U1 = ATTINY45 [package=dip]
  Sminus = Pushbutton [package="[THT]"]
  Smode = Pushbutton [package="[THT]"]
  M1 = MAX7219 8x8 single Led Matrix Module
  M2 = MAX7219 8x8 single Led Matrix Module
  M3 = MAX7219 8x8 single Led Matrix Module
  R1 = Resistor [tolerance=±5% resistance=10k power=0.25 package=THT]
  R3 = Resistor [tolerance=±5% resistance=56k power=0.25 package=THT]
  J1 = female pin header, 5 pins [form="♀ (female)"]
  J2 = male pin header, 5 pins [form="♂ (male)"]
  C2 = Ceramic Capacitor [capacitance=100nF voltage=10V package="100 mil [THT, multilayer]"]
  Sreset = Pushbutton [package="[THT]"]
  Splus = Pushbutton [package="[THT]"]
  R2 = Resistor [tolerance=±5% resistance=10k power=0.25 package=THT]
  J6 = male pin header, 4 pins [form="♂ (male)"]
  J7 = female pin header, 4 pins [form="♀ (female)"]
  U3 = V_REG_LD1117VXX [package=78xxl]
  J11 = female pin header, 1 pin [form="♀ (female)"]
  J12 = female pin header, 1 pin [form="♀ (female)"]
  U4 = V_REG_LD1117VXX [package=78xxl]
  C1 = Electrolytic Capacitor [capacitance=100µF voltage=35V package="100 mil [THT, electrolytic]"]
  J10 = female pin header, 4 pins [form="♀ (female)"]

nets:
  N1: ZS-042_RTC1.GND, J7.pin4
  N2: ZS-042_RTC1.VCC, J7.pin3
  J7: ZS-042_RTC1.SDA, J7.pin2
  J6: ZS-042_RTC1.SCL, J7.pin1
  N3: U1.PB5(NRES), Sreset.Pin_1, Sreset.Pin_2
  N4: U1.PB3(ADC3), Sminus.Pin_3, Sminus.Pin_4, Smode.Pin_3, Smode.Pin_4, R3.Pin_1, Splus.Pin_3, Splus.Pin_4
  J2: U1.PB4(ADC2), M1.I-CS-1, M1.O-CS-1, M1.I-CS-2, M1.O-CS-2, M1.I-CS-3, M1.O-CS-3, M1.I-CS-4, M1.O-CS-4, M2.I-CS-1, M2.O-CS-1, M2.I-CS-2, M2.O-CS-2, M2.I-CS-3, M2.O-CS-3, M2.I-CS-4, M2.O-CS-4, M3.I-CS-1, M3.O-CS-1, M3.I-CS-2, M3.O-CS-2, M3.I-CS-3, M3.O-CS-3, M3.I-CS-4, M3.O-CS-4, J1.pin2, J2.pin2
  GND/J4/J9: U1.GND, M1.I-GND-1, M1.O-GND-1, M1.I-GND-2, M1.O-GND-2, M1.I-GND-3, M1.O-GND-3, M1.I-GND-4, M1.O-GND-4, M2.I-GND-1, M2.O-GND-1, M2.I-GND-2, M2.O-GND-2, M2.I-GND-3, M2.O-GND-3, M2.I-GND-4, M2.O-GND-4, M3.I-GND-1, M3.O-GND-1, M3.I-GND-2, M3.O-GND-2, M3.I-GND-3, M3.O-GND-3, M3.I-GND-4, M3.O-GND-4, R3.Pin_0, J1.pin4, J2.pin4, C2.0, Sreset.Pin_3, Sreset.Pin_4, J6.pin4, U3.GND, J12.pin1, U4.GND, C1.-, J10.pin1
  J3: U1.PB0(MOSI), M3.I-DIN-1, J1.pin3, J2.pin3, J6.pin2
  J1: U1.PB1(MISO), M1.I-CLK-1, M1.O-CLK-1, M1.I-CLK-2, M1.O-CLK-2, M1.I-CLK-3, M1.O-CLK-3, M1.I-CLK-4, M1.O-CLK-4, M2.I-CLK-1, M2.O-CLK-1, M2.I-CLK-2, M2.O-CLK-2, M2.I-CLK-3, M2.O-CLK-3, M2.I-CLK-4, M2.O-CLK-4, M3.I-CLK-1, M3.O-CLK-1, M3.I-CLK-2, M3.O-CLK-2, M3.I-CLK-3, M3.O-CLK-3, M3.I-CLK-4, M3.O-CLK-4, J1.pin1, J2.pin1
  N5: U1.PB2(SCK_ADC1), J6.pin1
  +5V A/J8: U1.VCC, Smode.Pin_1, Smode.Pin_2, R2.Pin_1, J6.pin3, U4.OUT, J10.pin2
  N6: Sminus.Pin_1, Sminus.Pin_2, R1.Pin_0
  N7: M1.I-DIN-1, M3.O-DOUT-4
  +5V B/J5: M1.I-VCC-1, M1.O-VCC-1, M1.I-VCC-2, M1.O-VCC-2, M1.I-VCC-3, M1.O-VCC-3, M1.I-VCC-4, M1.O-VCC-4, M2.I-VCC-1, M2.O-VCC-1, M2.I-VCC-2, M2.O-VCC-2, M2.I-VCC-3, M2.O-VCC-3, M2.I-VCC-4, M2.O-VCC-4, M3.I-VCC-1, M3.O-VCC-1, M3.I-VCC-2, M3.O-VCC-2, M3.I-VCC-3, M3.O-VCC-3, M3.I-VCC-4, M3.O-VCC-4, J1.pin5, J2.pin5, C2.1, C1.+
  N8: M1.O-DOUT-1, M1.I-DIN-2
  N9: M1.O-DOUT-2, M1.I-DIN-3
  N10: M1.O-DOUT-3, M1.I-DIN-4
  N11: M1.O-DOUT-4, M2.I-DIN-1
  N12: M2.O-DOUT-1, M2.I-DIN-2
  N13: M2.O-DOUT-2, M2.I-DIN-3
  N14: M2.O-DOUT-3, M2.I-DIN-4
  N15: M3.O-DOUT-1, M3.I-DIN-2
  N16: M3.O-DOUT-2, M3.I-DIN-3
  N17: M3.O-DOUT-3, M3.I-DIN-4
  N18: R1.Pin_1, Splus.Pin_1, Splus.Pin_2, R2.Pin_0
  N19: U3.OUT, J10.pin4
  N20: U3.IN, J11.pin1, U4.IN

custom parts:
  MAX7219 8x8 single Led Matrix Module: Description: MAX7219 8x8 LedMatrix single Red Module Dimensions: 32x32mm Documents:
